// Logisim project RRISC.circ as structural Verilog: 6 circuits, main circuit main
module main (
);

  wire and_1_out, and_2_out, CARRY, comparator_1_eq, demultiplexer_1_out4, demultiplexer_1_out5,
       demultiplexer_1_out13, demultiplexer_2_out0, demultiplexer_2_out1, demultiplexer_2_out2,
       demultiplexer_2_out3, EX, INST_RB, INST_WB, INSTF, MEM_WRITE, or_1_out, pc_1_boutajump,
       pc_1_boutaskip, RST, WB, WRITEFLAG;
  wire [3:0] ACC_OUT_RX_WB, IMMEDIATE, OPCODE;
  wire [7:0] ALU_OUT_RESULT, MEM_DATA, MEMDATAIN, multiplexer_1_out, R0_ACC, RCD, RCS, register_1_q,
       register_2_q, register_3_q, register_4_q;
  wire [15:0] MEM_PC, REGS_OUT_MEM;

  Comparator #(.width(14)) comparator_1 (.a(14'h3c3c), .b(REGS_OUT_MEM[15:2]), .eq(comparator_1_eq));  // open: gt, lt
  PC pc_1 (
    .IN_MEMREG(REGS_OUT_MEM), .IN_RCS(RCS), .IN_RCD(RCD), .IN_IMMEDIATE(IMMEDIATE), .IN_OPCODE(OPCODE),
    .IN_WB(WB), .IN_RST(RST), .IN_CARRYFLAG(CARRY), .MEMPC(MEM_PC), .BOUTAJUMP(pc_1_boutajump),
    .BOUTASKIP(pc_1_boutaskip));
  LED led_1 (.in(pc_1_boutajump));
  LED led_2 (.in(pc_1_boutaskip));
  Demultiplexer #(.enable("false"), .select(4)) demultiplexer_1 (
    .out4(demultiplexer_1_out4), .out5(demultiplexer_1_out5), .out13(demultiplexer_1_out13), .in(1'b1),
    .sel(OPCODE));  // open: out0, out1, out2, out3, out6, out7, out8, out9, out10, out11, out12, out14, out15
  and and_1 (and_1_out, MEM_WRITE, comparator_1_eq);
  Demultiplexer #(.enable("false"), .select(2)) demultiplexer_2 (
    .out0(demultiplexer_2_out0), .out1(demultiplexer_2_out1), .out2(demultiplexer_2_out2),
    .out3(demultiplexer_2_out3), .in(and_1_out), .sel(REGS_OUT_MEM[1:0]));
  RAM #(.addrWidth(16), .clearpin("true"), .databus("bidir"), .trigger("high")) ram_1 (
    .addr(MEM_PC), .we(1'b0), .oe(1'b1), .data({OPCODE, IMMEDIATE}));  // open: clr
  RAM #(.addrWidth(16), .clearpin("true"), .databus("bidir"), .trigger("high")) ram_2 (
    .addr(REGS_OUT_MEM), .we(MEM_WRITE), .oe(INST_RB), .data(MEM_DATA), .clr(RST));
  or or_1 (or_1_out, demultiplexer_1_out4, demultiplexer_1_out5, demultiplexer_1_out13);
  Register register_1 (.D(MEMDATAIN), .en(demultiplexer_2_out0), .clk(WB), .Q(register_1_q), .clr(RST));
  Register register_2 (.D(MEMDATAIN), .en(demultiplexer_2_out1), .clk(WB), .Q(register_2_q), .clr(RST));
  Register register_3 (.D(MEMDATAIN), .en(demultiplexer_2_out2), .clk(WB), .Q(register_3_q), .clr(RST));
  Register register_4 (.D(MEMDATAIN), .en(demultiplexer_2_out3), .clk(WB), .Q(register_4_q), .clr(RST));
  Button BRST (.out(RST));
  and and_2 (and_2_out, WRITEFLAG, ~or_1_out);  // AND_Gate
  Multiplexer #(.enable("false"), .width(8)) multiplexer_1 (
    .in0(ALU_OUT_RESULT), .in1(MEM_DATA), .out(multiplexer_1_out), .sel(INST_RB));
  _7_Segment_Display u_7_segment_display_1 (
    .g(register_1_q[6]), .f(register_1_q[5]), .a(register_1_q[0]), .b(register_1_q[1]), .e(register_1_q[4]),
    .d(register_1_q[3]), .c(register_1_q[2]), .dp(register_1_q[7]));
  _7_Segment_Display u_7_segment_display_2 (
    .g(register_2_q[6]), .f(register_2_q[5]), .a(register_2_q[0]), .b(register_2_q[1]), .e(register_2_q[4]),
    .d(register_2_q[3]), .c(register_2_q[2]), .dp(register_2_q[7]));
  _7_Segment_Display u_7_segment_display_3 (
    .g(register_3_q[6]), .f(register_3_q[5]), .a(register_3_q[0]), .b(register_3_q[1]), .e(register_3_q[4]),
    .d(register_3_q[3]), .c(register_3_q[2]), .dp(register_3_q[7]));
  _7_Segment_Display u_7_segment_display_4 (
    .g(register_4_q[6]), .f(register_4_q[5]), .a(register_4_q[0]), .b(register_4_q[1]), .e(register_4_q[4]),
    .d(register_4_q[3]), .c(register_4_q[2]), .dp(register_4_q[7]));
  // Probe on multiplexer_1_out
  // Probe on ACC_OUT_RX_WB
  Controller controller_1 (.RST(RST), .EX(EX), .WB(WB), .WRITEFLAG(WRITEFLAG));  // open: INSTF
  and u_INST_RB (INST_RB, OPCODE[0], OPCODE[1], ~OPCODE[2], OPCODE[3]);  // AND_Gate
  and u_INST_WB (INST_WB, OPCODE[0], ~OPCODE[1], OPCODE[2], OPCODE[3]);  // AND_Gate
  and and_3 (MEM_WRITE, INST_WB, WRITEFLAG);
  // Probe on R0_ACC
  REGS regs_1 (
    .RST(RST), .Data(multiplexer_1_out), .CLK(WB), .Write(and_2_out), .Rx_Read(IMMEDIATE),
    .Rx_Write(ACC_OUT_RX_WB), .OUT_R0_ACC(R0_ACC), .OUT_REGDATA(MEMDATAIN), .OUT_RCS(RCS), .OUT_RCD(RCD),
    .OUT_MEM(REGS_OUT_MEM));
  // Probe on MEMDATAIN
  // Probe on RCS
  // Probe on RCD
  // Probe on REGS_OUT_MEM
  MuxALU muxalu_1 (
    .REGDATA(MEMDATAIN), .OPCODE(OPCODE), .IN_WB_FLAGS(WB), .IN_RST_FLAGS(RST), .IMMEDIATE(IMMEDIATE),
    .ACC(R0_ACC), .OUT_CARRY(CARRY), .OUT_RX_WB(ACC_OUT_RX_WB), .RESULT(ALU_OUT_RESULT));
  // Probe on R0_ACC
  // Probe on ALU_OUT_RESULT
  assign MEM_DATA = INST_WB ? MEMDATAIN : 8'bz;  // Controlled_Buffer controlled_buffer_1
  // Probe on ALU_OUT_RESULT
  Register u_INSTF (.en(1'b1), .clk(INSTF), .clr(RST));  // open: D, Q

  // Notes on the sheet:
  //   In=43 / Out=16
  //   Would be ANDed with its range,such as CE <= memory[13]
  //   An Example of Memory-Mapped IO
  //   11ns
  //   Every stage MUST effect state logic
  //   5ns 74as
  //   In=18 / Out=48
  //   24ns
  //   Hardware:
  //   e>c+30ns
  //   ~20 Registers
  //   1 64k SRAM
  //   ~50 logic gates
  //   ~20 ALU logic gates
  //   ~10 PC Board
  //   ~10 regfile logic gates
  //   ~6 MB logic gates
  //   ~5 MMIO SRAM
  //   40MHz = 25ns
  //   30MHz = 33.3ns
  //   25MHz = 40ns
  //   20MHz = 50ns
  //   15MHz = 66.6ns
  //   10MHz = 100ns
  //   ~40ns
  //   NOTE:Put Amplifier Here
  //   In=26 / Out=13
  //   EX: Spends cycle feeding-through ALU. Data clocked into WB at end.
  //   WE Pulled high for cycle. Writes to registers. Writes to memory if inst_memwrite
  //   <- Expected 16MHz
  //   <- Test around 1kHz
  //   Something that could drive ~10 chips
  //   34:14
endmodule

module ALU (
  input  [7:0] IN_ACC,
  input  [3:0] OPCODE,
  input  [3:0] IN_IMMEDIATE,
  input  [7:0] REGDATA,
  input  IN_WB_FLAGS,
  input  IN_RST_FLAGS,
  output [7:0] OUT_RESULT,
  output [3:0] OUT_RX_WB,
  output OUT_CARRY
);

  wire and_1_out, and_2_out, demultiplexer_1_out2, demultiplexer_1_out4, demultiplexer_1_out5, FLAG_CARRY_IN,
       nor_1_out, not_1_out, or_1_out, or_3_out;
  wire [3:0] bit_extender_1_out, bit_extender_2_out;
  wire [7:0] adder_1_out, and_4_out, bit_extender_3_out, FULL_IMM, multiplexer_2_out, multiplexer_3_out,
       or_2_out, undriven, xor_1_out, xor_2_out;

  and and_1 (and_1_out, OPCODE[0], OPCODE[1], OPCODE[2]);
  and and_2 (and_2_out, OPCODE[1], OPCODE[2], OPCODE[3]);
  assign bit_extender_1_out = {{3{OPCODE[2]}}, OPCODE[2]};  // Bit_Extender bit_extender_1
  or or_1 (or_1_out, and_1_out, and_2_out);
  Multiplexer #(.enable("false"), .width(8)) multiplexer_1 (
    .in0({bit_extender_1_out, IN_IMMEDIATE}), .in1(REGDATA), .out(FULL_IMM), .sel(OPCODE[0]));
  assign bit_extender_2_out = {{3{or_1_out}}, or_1_out};  // Bit_Extender bit_extender_2
  assign OUT_RX_WB = IN_IMMEDIATE & bit_extender_2_out;  // AND_Gate and_3, 4 bits wide
  assign bit_extender_3_out = {{7{OPCODE[1]}}, OPCODE[1]};  // Bit_Extender bit_extender_3
  assign xor_1_out = bit_extender_3_out ^ FULL_IMM;  // XOR_Gate xor_1, 8 bits wide
  Adder adder_1 (.a(IN_ACC), .b(xor_1_out), .out(adder_1_out), .cin(OPCODE[1]), .cout(FLAG_CARRY_IN));
  assign and_4_out = IN_ACC & FULL_IMM;  // AND_Gate and_4, 8 bits wide
  Multiplexer #(.enable("false"), .width(8)) multiplexer_2 (
    .in0(REGDATA), .in1(IN_ACC), .out(multiplexer_2_out), .sel(OPCODE[0]));
  assign or_2_out = IN_ACC | FULL_IMM;  // OR_Gate or_2, 8 bits wide
  assign xor_2_out = IN_ACC ^ FULL_IMM;  // XOR_Gate xor_2, 8 bits wide
  nor nor_1 (nor_1_out, OPCODE[3], OPCODE[2]);
  Register #(.width(1)) FLAG_CARRY (
    .D(FLAG_CARRY_IN), .en(nor_1_out), .clk(IN_WB_FLAGS), .Q(OUT_CARRY), .clr(IN_RST_FLAGS));
  Multiplexer #(.enable("false"), .select(3), .width(8)) multiplexer_3 (
    .in0(adder_1_out), .in1(adder_1_out), .in2(and_4_out), .in3(multiplexer_2_out), .in4(or_2_out),
    .in5(xor_2_out), .in6(IN_ACC), .in7(undriven), .out(multiplexer_3_out), .sel(OPCODE[3:1]));
  not not_1 (not_1_out, OPCODE[0]);
  Demultiplexer #(.enable("false"), .select(3)) demultiplexer_1 (
    .out2(demultiplexer_1_out2), .out4(demultiplexer_1_out4), .out5(demultiplexer_1_out5), .in(not_1_out),
    .sel(OPCODE[3:1]));  // open: out0, out1, out3, out6, out7
  Multiplexer #(.enable("false"), .width(8)) multiplexer_4 (
    .in0(multiplexer_3_out), .in1({multiplexer_3_out[3:0], multiplexer_3_out[7:4]}), .out(OUT_RESULT),
    .sel(or_3_out));
  or or_3 (or_3_out, demultiplexer_1_out2, demultiplexer_1_out4, demultiplexer_1_out5);

  // Other names for the same wires on the sheet: IMMEDIATE[3:0] = IN_IMMEDIATE; OPCODE_LSB = OPCODE[0];
  //   OPCODE_BIT1 = OPCODE[1]

  // Notes on the sheet:
  //   If set, WB, or RB instruction: (DST=IMM) ELSE (DST=ACC)
  //   Data is register or immediate. The 4MSB of imm are 1s for AND and 0s for xor,add,or
  //   ANDI/AND
  //   GET/SET
  //   ORI/OR
  //   XORI/XOR
  //   WE = add/sub = opcode 0-3
  //   The actual ALU
  //   18.5ns
  //   ADDI/ADD/SUBI/SUB
  //   Has RST or WE
  //   SIF/JIF
  //   RB/WB
  //   14ns - 74HCS151
  //   Swap nibbles on imm and,or,xor
  //   Actual ALU Stuff
  //   ~40ns
endmodule

module REGS (
  input  RST,
  input  [7:0] Data,
  input  CLK,
  input  Write,
  input  [3:0] Rx_Read,
  input  [3:0] Rx_Write,
  output [7:0] OUT_R0_ACC,
  output [7:0] OUT_REGDATA,
  output [7:0] OUT_RCS,
  output [7:0] OUT_RCD,
  output [15:0] OUT_MEM
);

  wire demultiplexer_1_out0, demultiplexer_1_out1, demultiplexer_1_out2, demultiplexer_1_out3,
       demultiplexer_1_out4, demultiplexer_1_out5, demultiplexer_1_out6, demultiplexer_1_out7,
       demultiplexer_1_out8, demultiplexer_1_out9, demultiplexer_1_out10, demultiplexer_1_out11,
       demultiplexer_1_out12, demultiplexer_1_out13, demultiplexer_1_out14, demultiplexer_1_out15;
  wire [7:0] R1_q, R2_q, R3_q, R4_q, R5_q, R6_q, R7_q, R8_q, R9_RAT_q, RA_RSH_q, RB_RSL_q;

  Demultiplexer #(.enable("false"), .select(4)) demultiplexer_1 (
    .out0(demultiplexer_1_out0), .out1(demultiplexer_1_out1), .out2(demultiplexer_1_out2),
    .out3(demultiplexer_1_out3), .out4(demultiplexer_1_out4), .out5(demultiplexer_1_out5),
    .out6(demultiplexer_1_out6), .out7(demultiplexer_1_out7), .out8(demultiplexer_1_out8),
    .out9(demultiplexer_1_out9), .out10(demultiplexer_1_out10), .out11(demultiplexer_1_out11),
    .out12(demultiplexer_1_out12), .out13(demultiplexer_1_out13), .out14(demultiplexer_1_out14),
    .out15(demultiplexer_1_out15), .in(Write), .sel(Rx_Write));
  Register R0_ACC (.D(Data), .en(demultiplexer_1_out0), .clk(CLK), .Q(OUT_R0_ACC), .clr(RST));
  Register R1 (.D(Data), .en(demultiplexer_1_out1), .clk(CLK), .Q(R1_q), .clr(RST));
  Register R2 (.D(Data), .en(demultiplexer_1_out2), .clk(CLK), .Q(R2_q), .clr(RST));
  Register R3 (.D(Data), .en(demultiplexer_1_out3), .clk(CLK), .Q(R3_q), .clr(RST));
  Register R4 (.D(Data), .en(demultiplexer_1_out4), .clk(CLK), .Q(R4_q), .clr(RST));
  Register R5 (.D(Data), .en(demultiplexer_1_out5), .clk(CLK), .Q(R5_q), .clr(RST));
  Register R6 (.D(Data), .en(demultiplexer_1_out6), .clk(CLK), .Q(R6_q), .clr(RST));
  Register R7 (.D(Data), .en(demultiplexer_1_out7), .clk(CLK), .Q(R7_q), .clr(RST));
  Register R8 (.D(Data), .en(demultiplexer_1_out8), .clk(CLK), .Q(R8_q), .clr(RST));
  Register R9_RAT (.D(Data), .en(demultiplexer_1_out9), .clk(CLK), .Q(R9_RAT_q), .clr(RST));
  Register RA_RSH (.D(Data), .en(demultiplexer_1_out10), .clk(CLK), .Q(RA_RSH_q), .clr(RST));
  Register RB_RSL (.D(Data), .en(demultiplexer_1_out11), .clk(CLK), .Q(RB_RSL_q), .clr(RST));
  Register RC_RCS (.D(Data), .en(demultiplexer_1_out12), .clk(CLK), .Q(OUT_RCS), .clr(RST));
  Register RD_RCD (.D(Data), .en(demultiplexer_1_out13), .clk(CLK), .Q(OUT_RCD), .clr(RST));
  Register RE_RMH (.D(Data), .en(demultiplexer_1_out14), .clk(CLK), .Q(OUT_MEM[15:8]), .clr(RST));
  Register RF_RML (.D(Data), .en(demultiplexer_1_out15), .clk(CLK), .Q(OUT_MEM[7:0]), .clr(RST));
  Multiplexer #(.enable("false"), .select(4), .width(8)) multiplexer_1 (
    .in0(OUT_R0_ACC), .in1(R1_q), .in2(R2_q), .in3(R3_q), .in4(R4_q), .in5(R5_q), .in6(R6_q), .in7(R7_q),
    .in8(R8_q), .in9(R9_RAT_q), .in10(RA_RSH_q), .in11(RB_RSL_q), .in12(OUT_RCS), .in13(OUT_RCD),
    .in14(OUT_MEM[15:8]), .in15(OUT_MEM[7:0]), .out(OUT_REGDATA), .sel(Rx_Read));

  // Notes on the sheet:
  //   7xx154
  //   30ns
  //   6ns
  //   Has WE no RST, such as 74xx 377
  //   8x  7xx250
  //   Is actually 8 16:1 muxes
endmodule

module Controller (
  input  RST,
  output INSTF,
  output EX,
  output WB,
  output WRITEFLAG
);

  wire clock_1_out, clock_2_out, d_ff_1_q, d_ff_3_q, d_ff_5_q, d_ff_6_q, undriven;

  Clock clock_1 (.out(clock_1_out));
  D_Flip_Flop d_ff_1 (.D(d_ff_5_q), .clk(clock_2_out), .Q(d_ff_1_q), .preset(undriven));  // open: Qn, reset
  Clock clock_2 (.out(clock_2_out));
  D_Flip_Flop d_ff_2 (.D(WB), .clk(clock_1_out), .Q(EX), .preset(RST));  // open: Qn, reset
  D_Flip_Flop d_ff_3 (.D(d_ff_1_q), .clk(clock_2_out), .Q(d_ff_3_q), .reset(undriven));  // open: Qn, preset
  D_Flip_Flop d_ff_4 (.D(EX), .clk(clock_1_out), .Q(WB), .reset(RST));  // open: Qn, preset
  D_Flip_Flop d_ff_5 (.D(d_ff_3_q), .clk(clock_2_out), .Q(d_ff_5_q), .reset(undriven));  // open: Qn, preset
  D_Flip_Flop #(.trigger("falling")) d_ff_6 (
    .D(d_ff_3_q), .clk(clock_2_out), .Q(d_ff_6_q), .reset(undriven));  // open: Qn, preset
  D_Flip_Flop #(.trigger("falling")) d_ff_7 (
    .D(EX), .clk(clock_1_out), .Q(WRITEFLAG), .reset(RST));  // open: Qn, preset
endmodule

module PC (
  input  [15:0] IN_MEMREG,
  input  [7:0] IN_RCS,
  input  [7:0] IN_RCD,
  input  [3:0] IN_IMMEDIATE,
  input  [3:0] IN_OPCODE,
  input  IN_WB,
  input  IN_RST,
  input  IN_CARRYFLAG,
  output [15:0] MEMPC,
  output BOUTAJUMP,
  output BOUTASKIP
);

  wire and_1_out, and_2_out, comparator_1_eq, comparator_1_gt, comparator_1_lt, multiplexer_1_out, or_1_out,
       xor_1_out;
  wire [0:0] not_1_out;
  wire [15:0] adder_1_out, multiplexer_2_out;

  Comparator #(.mode("unsigned")) comparator_1 (
    .a(IN_RCS), .b(IN_RCD), .gt(comparator_1_gt), .eq(comparator_1_eq), .lt(comparator_1_lt));
  or or_1 (or_1_out, IN_RCS[0], IN_RCS[1], IN_RCS[2], IN_RCS[3], IN_RCS[4], IN_RCS[5], IN_RCS[6], IN_RCS[7]);
  Multiplexer #(.enable("false"), .select(3)) multiplexer_1 (
    .in0(1'b1), .in1(or_1_out), .in2(IN_RCS[7]), .in3(comparator_1_lt), .in4(comparator_1_eq),
    .in5(comparator_1_gt), .in6(IN_RCS[0]), .in7(IN_CARRYFLAG), .out(multiplexer_1_out),
    .sel(IN_IMMEDIATE[3:1]));
  xor xor_1 (xor_1_out, multiplexer_1_out, IN_IMMEDIATE[0]);
  Multiplexer #(.enable("false"), .width(16)) multiplexer_2 (
    .in0(adder_1_out), .in1(IN_MEMREG), .out(multiplexer_2_out), .sel(BOUTAJUMP));
  not not_1 (not_1_out[0], BOUTASKIP);
  and and_1 (and_1_out, ~IN_OPCODE[3], IN_OPCODE[2], ~IN_OPCODE[1], IN_OPCODE[0]);  // AND_Gate
  and and_2 (and_2_out, ~IN_OPCODE[3], IN_OPCODE[2], ~IN_OPCODE[1], ~IN_OPCODE[0]);  // AND_Gate
  Register #(.width(16)) register_1 (.D(multiplexer_2_out), .en(1'b1), .clk(IN_WB), .Q(MEMPC), .clr(IN_RST));
  Adder #(.width(16)) adder_1 (
    .a(MEMPC), .b({{14{1'b0}}, BOUTASKIP, not_1_out[0]}), .out(adder_1_out));  // open: cin, cout
  and and_3 (BOUTAJUMP, xor_1_out, and_1_out);
  and and_4 (BOUTASKIP, xor_1_out, and_2_out);

  // Other names for the same wires on the sheet: ACC_OUT_IS_SKIP = BOUTASKIP; ACC_OUT_IS_JUMP = BOUTAJUMP;
  //   FLAG_CARRY_OUT = IN_CARRYFLAG; IMMEDIATE[3:0] = IN_IMMEDIATE; OPCODE[3:0] = IN_OPCODE;
  //   REGS_OUT_MEM[15:0] = IN_MEMREG

  // Notes on the sheet:
  //   Such as a 74xx 684 with a NAND for >
  //   Conditional Jump
  //   12ns
  //   17ns
  //   Branch Event
  //   On actual program counter, opcode parsing is done by the motherboard. This will recieve a is_jmp and is_skip and will parse from there
  //   Branch event and instruction
  //   34ns - 74xx283
  //   PC+1 or PC+2
  //   5ns
  //   ~40ns
  //   Has RST no WE, such as 74xx 273
endmodule

module MuxALU (
  input  [7:0] REGDATA,
  input  [3:0] OPCODE,
  input  IN_WB_FLAGS,
  input  IN_RST_FLAGS,
  input  [3:0] IMMEDIATE,
  input  [7:0] ACC,
  output OUT_CARRY,
  output [3:0] OUT_RX_WB,
  output [7:0] RESULT
);

  wire adder_1_cout, and_2_out, and_3_out, and_5_out, demultiplexer_1_out3, demultiplexer_1_out4,
       demultiplexer_1_out7, L, nor_1_out, not_1_out, not_2_out, not_3_out, SWAPNIBBLES;
  wire [3:0] bit_extender_1_out, bit_extender_2_out, R;
  wire [7:0] adder_1_out, multiplexer_1_out, multiplexer_2_out, OPB;

  not not_1 (not_1_out, OPCODE[2]);
  not not_2 (not_2_out, OPCODE[3]);
  Multiplexer #(.enable("false"), .select(2)) multiplexer_1 (
    .in0(R[0]), .in1(OPCODE[1]), .in2(R[2]), .in3(R[3]), .out(multiplexer_1_out[0]), .sel({OPB[0], ACC[0]}));
  Multiplexer #(.select(2)) multiplexer_2 (
    .in0(1'b0), .in1(1'b1), .in2(1'b0), .in3(1'b1), .out(multiplexer_2_out[0]), .sel({OPB[0], ACC[0]}), .en(L));
  not not_3 (not_3_out, OPCODE[1]);
  and and_1 (L, not_1_out, not_2_out);
  and and_2 (and_2_out, OPCODE[3], not_3_out);
  and and_3 (and_3_out, not_3_out, L);
  Multiplexer #(.enable("false"), .select(2)) multiplexer_3 (
    .in0(R[0]), .in1(OPCODE[1]), .in2(R[2]), .in3(R[3]), .out(multiplexer_1_out[1]), .sel({OPB[1], ACC[1]}));
  Multiplexer #(.select(2)) multiplexer_4 (
    .in0(1'b0), .in1(1'b1), .in2(1'b0), .in3(1'b1), .out(multiplexer_2_out[1]), .sel({OPB[1], ACC[1]}), .en(L));
  and and_4 (R[0], L, OPCODE[1]);
  or or_1 (R[2], OPCODE[2], and_3_out);
  or or_2 (R[3], and_3_out, OPCODE[3]);
  Multiplexer #(.enable("false"), .select(2)) multiplexer_5 (
    .in0(R[0]), .in1(OPCODE[1]), .in2(R[2]), .in3(R[3]), .out(multiplexer_1_out[2]), .sel({OPB[2], ACC[2]}));
  Multiplexer #(.select(2)) multiplexer_6 (
    .in0(1'b0), .in1(1'b1), .in2(1'b0), .in3(1'b1), .out(multiplexer_2_out[2]), .sel({OPB[2], ACC[2]}), .en(L));
  assign bit_extender_1_out = {{3{and_2_out}}, and_2_out};  // Bit_Extender bit_extender_1
  Multiplexer #(.enable("false"), .select(2)) multiplexer_7 (
    .in0(R[0]), .in1(OPCODE[1]), .in2(R[2]), .in3(R[3]), .out(multiplexer_1_out[3]), .sel({OPB[3], ACC[3]}));
  Multiplexer #(.select(2)) multiplexer_8 (
    .in0(1'b0), .in1(1'b1), .in2(1'b0), .in3(1'b1), .out(multiplexer_2_out[3]), .sel({OPB[3], ACC[3]}), .en(L));
  Multiplexer #(.enable("false"), .select(2)) multiplexer_9 (
    .in0(R[0]), .in1(OPCODE[1]), .in2(R[2]), .in3(R[3]), .out(multiplexer_1_out[4]), .sel({OPB[4], ACC[4]}));
  Multiplexer #(.select(2)) multiplexer_10 (
    .in0(1'b0), .in1(1'b1), .in2(1'b0), .in3(1'b1), .out(multiplexer_2_out[4]), .sel({OPB[4], ACC[4]}), .en(L));
  Multiplexer #(.enable("false"), .width(8)) multiplexer_11 (
    .in0(REGDATA), .in1({bit_extender_1_out, IMMEDIATE}), .out(OPB), .sel(OPCODE[0]));
  and and_5 (and_5_out, OPCODE[1], ~OPCODE[2], OPCODE[3]);  // AND_Gate
  assign bit_extender_2_out = {{3{and_5_out}}, and_5_out};  // Bit_Extender bit_extender_2
  Multiplexer #(.enable("false"), .select(2)) multiplexer_12 (
    .in0(R[0]), .in1(OPCODE[1]), .in2(R[2]), .in3(R[3]), .out(multiplexer_1_out[5]), .sel({OPB[5], ACC[5]}));
  Multiplexer #(.select(2)) multiplexer_13 (
    .in0(1'b0), .in1(1'b1), .in2(1'b0), .in3(1'b1), .out(multiplexer_2_out[5]), .sel({OPB[5], ACC[5]}), .en(L));
  assign OUT_RX_WB = IMMEDIATE & bit_extender_2_out;  // AND_Gate and_6, 4 bits wide
  Demultiplexer #(.enable("false"), .select(3)) demultiplexer_1 (
    .out3(demultiplexer_1_out3), .out4(demultiplexer_1_out4), .out7(demultiplexer_1_out7), .in(OPCODE[0]),
    .sel(OPCODE[3:1]));  // open: out0, out1, out2, out5, out6
  Multiplexer #(.enable("false"), .select(2)) multiplexer_14 (
    .in0(R[0]), .in1(OPCODE[1]), .in2(R[2]), .in3(R[3]), .out(multiplexer_1_out[6]), .sel({OPB[6], ACC[6]}));
  Multiplexer #(.select(2)) multiplexer_15 (
    .in0(1'b0), .in1(1'b1), .in2(1'b0), .in3(1'b1), .out(multiplexer_2_out[6]), .sel({OPB[6], ACC[6]}), .en(L));
  or or_3 (SWAPNIBBLES, demultiplexer_1_out3, demultiplexer_1_out4, demultiplexer_1_out7);
  Multiplexer #(.enable("false"), .select(2)) multiplexer_16 (
    .in0(R[0]), .in1(OPCODE[1]), .in2(R[2]), .in3(R[3]), .out(multiplexer_1_out[7]), .sel({OPB[7], ACC[7]}));
  Multiplexer #(.select(2)) multiplexer_17 (
    .in0(1'b0), .in1(1'b1), .in2(1'b0), .in3(1'b1), .out(multiplexer_2_out[7]), .sel({OPB[7], ACC[7]}), .en(L));
  Adder adder_1 (.a(multiplexer_1_out), .b(multiplexer_2_out), .out(adder_1_out), .cin(R[0]), .cout(adder_1_cout));
  Multiplexer #(.enable("false"), .width(8)) multiplexer_18 (
    .in0(adder_1_out), .in1({adder_1_out[3:0], adder_1_out[7:4]}), .out(RESULT), .sel(SWAPNIBBLES));
  nor nor_1 (nor_1_out, OPCODE[3], OPCODE[2]);
  Register #(.width(1)) register_1 (
    .D(adder_1_cout), .en(nor_1_out), .clk(IN_WB_FLAGS), .Q(OUT_CARRY), .clr(IN_RST_FLAGS));

  // Other names for the same wires on the sheet: OPCODE_LSB = OPCODE[0]; R[1] = OPCODE[1]

  // Notes on the sheet:
  //   -------------------------------------- Note: On physical ALU, all objects above this text line will happen on the motherboard --------------------------------------
  //   If set or rb instruction: (DST=IMM) ELSE (DST=ACC)
  //   Swap nibbles on imm and,or,xor
  //   WE = add/sub = opcode 0-3
endmodule
